# Fritzing sketch scheme (saved by Fritzing 0.9.4)
breadboards: 1

parts:
  J1 = Basic Servo
  J2 = Basic Servo
  Компонент1 = Arduino Uno (Rev3)

nets:
  GND: J1.gnd, J2.gnd, Компонент1.GND
  VCC: J1.vcc, J2.vcc, Компонент1.5V
  N1: J1.pulse, Компонент1.D10_PWM/SS
  N2: J2.pulse, Компонент1.D9_PWM
